# Fritzing sketch megashift (saved by Fritzing 0.8.7b)
circuit board: 21.045cm x 11.3875cm
breadboards: 3

parts:
  Arduino_Mega_2560_(Rev_3) = Arduino Mega 2560 (Rev3)
  Register_18 = 74HC595 [package="DIP16 [THT]"]
  Register_1 = 74HC595 [package="DIP16 [THT]"]
  Register_2 = 74HC595 [package="DIP16 [THT]"]
  Register_3 = 74HC595 [package="DIP16 [THT]"]
  Register_4 = 74HC595 [package="DIP16 [THT]"]
  Register_5 = 74HC595 [package="DIP16 [THT]"]
  Register_6 = 74HC595 [package="DIP16 [THT]"]
  Register_7 = 74HC595 [package="DIP16 [THT]"]
  Register_8 = 74HC595 [package="DIP16 [THT]"]
  Register_9 = 74HC595 [package="DIP16 [THT]"]
  Register_10 = 74HC595 [package="DIP16 [THT]"]
  Register_11 = 74HC595 [package="DIP16 [THT]"]
  Register_12 = 74HC595 [package="DIP16 [THT]"]
  Register_13 = 74HC595 [package="DIP16 [THT]"]
  Register_14 = 74HC595 [package="DIP16 [THT]"]
  Register_15 = 74HC595 [package="DIP16 [THT]"]
  Register_16 = 74HC595 [package="DIP16 [THT]"]
  Register_17 = 74HC595 [package="DIP16 [THT]"]

nets:
  N1: Arduino_Mega_2560_(Rev_3).D21/SCL, Arduino_Mega_2560_(Rev_3).SCL, Register_8.DS
  N2: Arduino_Mega_2560_(Rev_3).D20/SDA, Arduino_Mega_2560_(Rev_3).SDA, Register_7.SH_CP
  N3: Arduino_Mega_2560_(Rev_3).D19/RX1, Register_7.ST_CP
  N4: Arduino_Mega_2560_(Rev_3).D18/TX1, Register_7.DS
  N5: Arduino_Mega_2560_(Rev_3).D17_PWM/RX2, Register_6.SH_CP
  N6: Arduino_Mega_2560_(Rev_3).D16_PWM/TX2, Register_6.ST_CP
  N7: Arduino_Mega_2560_(Rev_3).D15/RX3, Register_6.DS
  N8: Arduino_Mega_2560_(Rev_3).D14/TX3, Register_5.SH_CP
  GND: Arduino_Mega_2560_(Rev_3).GND, Register_18.GND, Register_18.OE, Register_1.GND, Register_1.OE, Register_2.GND, Register_2.OE, Register_3.GND, Register_3.OE, Register_4.GND, Register_4.OE, Register_5.GND, Register_5.OE, Register_6.GND, Register_6.OE, Register_7.GND, Register_7.OE, Register_8.GND, Register_8.OE, Register_9.GND, Register_9.OE, Register_10.GND, Register_10.OE, Register_11.GND, Register_11.OE, Register_12.GND, Register_12.OE, Register_13.GND, Register_13.OE, Register_14.GND, Register_14.OE, Register_15.GND, Register_15.OE, Register_16.GND, Register_16.OE, Register_17.GND, Register_17.OE
  N9: Arduino_Mega_2560_(Rev_3).D13_PWM, Register_5.ST_CP
  N10: Arduino_Mega_2560_(Rev_3).D12_PWM, Register_5.DS
  N11: Arduino_Mega_2560_(Rev_3).D11_PWM, Register_4.SH_CP
  N12: Arduino_Mega_2560_(Rev_3).D10_PWM, Register_4.ST_CP
  N13: Arduino_Mega_2560_(Rev_3).D9_PWM, Register_4.DS
  N14: Arduino_Mega_2560_(Rev_3).D8_PWM, Register_3.SH_CP
  VCC: Arduino_Mega_2560_(Rev_3).5V, Register_18.MR, Register_18.VCC, Register_1.MR, Register_1.VCC, Register_2.MR, Register_2.VCC, Register_3.MR, Register_3.VCC, Register_4.MR, Register_4.VCC, Register_5.MR, Register_5.VCC, Register_6.MR, Register_6.VCC, Register_7.MR, Register_7.VCC, Register_8.MR, Register_8.VCC, Register_9.MR, Register_9.VCC, Register_10.MR, Register_10.VCC, Register_11.MR, Register_11.VCC, Register_12.MR, Register_12.VCC, Register_13.MR, Register_13.VCC, Register_14.MR, Register_14.VCC, Register_15.MR, Register_15.VCC, Register_16.MR, Register_16.VCC, Register_17.MR, Register_17.VCC
  N15: Arduino_Mega_2560_(Rev_3).D0_RX0, Register_1.DS
  N16: Arduino_Mega_2560_(Rev_3).D1_TX0, Register_1.ST_CP
  N17: Arduino_Mega_2560_(Rev_3).D2_PWM, Register_1.SH_CP
  N18: Arduino_Mega_2560_(Rev_3).D3_PWM, Register_2.DS
  N19: Arduino_Mega_2560_(Rev_3).D4_PWM, Register_2.ST_CP
  N20: Arduino_Mega_2560_(Rev_3).D5_PWM, Register_2.SH_CP
  N21: Arduino_Mega_2560_(Rev_3).D6_PWM, Register_3.DS
  N22: Arduino_Mega_2560_(Rev_3).D7_PWM, Register_3.ST_CP
  N23: Arduino_Mega_2560_(Rev_3).D22, Register_8.ST_CP
  N24: Arduino_Mega_2560_(Rev_3).D23, Register_8.SH_CP
  N25: Arduino_Mega_2560_(Rev_3).D24, Register_9.DS
  N26: Arduino_Mega_2560_(Rev_3).D25, Register_9.ST_CP
  N27: Arduino_Mega_2560_(Rev_3).D26, Register_9.SH_CP
  N28: Arduino_Mega_2560_(Rev_3).D27, Register_10.DS
  N29: Arduino_Mega_2560_(Rev_3).D28, Register_10.ST_CP
  N30: Arduino_Mega_2560_(Rev_3).D29, Register_10.SH_CP
  N31: Arduino_Mega_2560_(Rev_3).D30, Register_11.DS
  N32: Arduino_Mega_2560_(Rev_3).D31, Register_11.ST_CP
  N33: Arduino_Mega_2560_(Rev_3).D32, Register_11.SH_CP
  N34: Arduino_Mega_2560_(Rev_3).D33, Register_12.DS
  N35: Arduino_Mega_2560_(Rev_3).D34, Register_12.ST_CP
  N36: Arduino_Mega_2560_(Rev_3).D35, Register_12.SH_CP
  N37: Arduino_Mega_2560_(Rev_3).D36, Register_13.DS
  N38: Arduino_Mega_2560_(Rev_3).D37, Register_13.ST_CP
  N39: Arduino_Mega_2560_(Rev_3).D38, Register_13.SH_CP
  N40: Arduino_Mega_2560_(Rev_3).D39, Register_14.DS
  N41: Arduino_Mega_2560_(Rev_3).D40, Register_14.ST_CP
  N42: Arduino_Mega_2560_(Rev_3).D41, Register_14.SH_CP
  N43: Arduino_Mega_2560_(Rev_3).D42, Register_15.DS
  N44: Arduino_Mega_2560_(Rev_3).D43, Register_15.ST_CP
  N45: Arduino_Mega_2560_(Rev_3).D44, Register_15.SH_CP
  N46: Arduino_Mega_2560_(Rev_3).D45, Register_16.DS
  N47: Arduino_Mega_2560_(Rev_3).D46, Register_16.ST_CP
  N48: Arduino_Mega_2560_(Rev_3).D47, Register_16.SH_CP
  N49: Arduino_Mega_2560_(Rev_3).D48, Register_17.DS
  N50: Arduino_Mega_2560_(Rev_3).D49, Register_17.ST_CP
  N51: Arduino_Mega_2560_(Rev_3).D50, Register_17.SH_CP
  N52: Arduino_Mega_2560_(Rev_3).D51, Register_18.DS
  N53: Arduino_Mega_2560_(Rev_3).D52, Register_18.ST_CP
  N54: Arduino_Mega_2560_(Rev_3).D53, Register_18.SH_CP

notes:
  Electrorchestrion - Organic
  Copyright 2020 Gabriel Peressini
  All rights reserved.
