# Fritzing sketch monstermega2 (saved by Fritzing 0.9.4)
circuit board: 25.61cm x 9.93915cm

parts:
  ATmega_2560_16au = ATMEGA2560 [package=tqfp]
  ICSP = AVR ISP 6 Pin [package=2x3-ns]
  ICSP_U2 = AVR ISP 6 Pin [package=2x3-ns]
  R1 = Resistor [tolerance=±5% resistance=10k package="1206 [SMD]"]
  D1 = smd LED [color="Red (633nm)" package="1206 [SMD]"]
  R2 = Resistor [tolerance=±5% resistance=1k package="0603 [SMD]"]
  R3 = Resistor [tolerance=±5% resistance=1k package="0603 [SMD]"]
  USB_b = USB+SHIELD [package=usb-b-pth]
  Z1 = VARISTOR [package=0603-res]
  Z2 = VARISTOR [package=0603-res]
  C1 = Capacitor [package=0805]
  L1 = Inductors [package=0805]
  C2 = Capacitor [package=0603-cap]
  F1 = Resettable Fuse PTC [package=ptc-1206]
  C3 = Capacitor [package=0603-cap]
  LED1 = smd LED [color="Yellow (585nm)" package="0603 [SMD]"]
  R6 = Resistor [tolerance=±5% resistance=1k package="0603 [SMD]"]
  LED2 = smd LED [color="Yellow (585nm)" package="0603 [SMD]"]
  R7 = Resistor [tolerance=±5% resistance=1k package="0603 [SMD]"]
  U2 = Voltage Regulator LDO [package=sot23-5]
  VIN_GND = female pin header, 2 pins [form="♀ (female)"]
  R8 = Resistor [tolerance=±5% resistance=10k package="1206 [SMD]"]
  R9 = Resistor [tolerance=±5% resistance=10k package="1206 [SMD]"]
  C4 = Capacitor [package=0603-cap]
  R4 = Resistor [tolerance=±5% resistance=220 package="0402 [SMD]"]
  R5 = Resistor [tolerance=±5% resistance=220 package="0402 [SMD]"]
  U3 = LMV358 [package=so08]
  C5 = Capacitor [package=0603-cap]
  U4 = MOSFET-PCHANNEL [package=sot23-3]
  C6 = Capacitor [package=0805]
  RESET-EN = female pin header, 2 pins [form="♀ (female)"]
  C7 = Capacitor [package=0603-cap]
  R10 = Resistor [tolerance=±5% resistance=1k package="0603 [SMD]"]
  XTAL1 = Crystal [frequency="16 Mhz" package=THT]
  R11 = Resistor [tolerance=±5% resistance=1M package="0805 [SMD]"]
  C8 = Capacitor [package=0805]
  C9 = Capacitor [package=0805]
  U5 = LMV358 [package=so08]
  R12 = Resistor [tolerance=±5% resistance=1k package="0603 [SMD]"]
  LED3 = smd LED [color="Yellow (585nm)" package="0603 [SMD]"]
  LED4 = smd LED [color="Green (555nm)" package="0603 [SMD]"]
  R13 = Resistor [tolerance=±5% resistance=1k package="0603 [SMD]"]
  R14 = Resistor [tolerance=±5% resistance=1M package="0805 [SMD]"]
  U6 = Resonator [package=resonator-pth]
  C10 = Capacitor [package=0603-cap]
  C11 = Capacitor [package=0603-cap]
  C12 = Capacitor [package=0603-cap]
  C13 = Capacitor [package=0603-cap]
  R16 = Resistor [tolerance=±5% resistance=10k package="1206 [SMD]"]
  R15 = Resistor [tolerance=±5% resistance=10k package="1206 [SMD]"]
  D2 = smd LED [color="Red (633nm)" package="1206 [SMD]"]
  R17 = Resistor [tolerance=±5% resistance=10k package="1206 [SMD]"]
  C14 = Capacitor [package=0805]
  U7 = ATmega16U2 [package=QFN-32]
  pin_1_pin_2 = double row female pin header, 4 pins [form="♀ (female)"]
  J256 = double row female pin header, 16 pins [form="♀ (female)"]
  J48 = double row male pin header, 14 pins [form="♂ (male)"]
  RESET = Pushbutton [package="[SMD]"]
  J257 = double row male pin header, 30 pins [form="♂ (male)"]
  J260 = double row female pin header, 8 pins [form="♀ (female)"]
  Register_10 = 74HC595 SMD [package="SO16 [SMD]"]
  J261 = double row female pin header, 8 pins [form="♀ (female)"]
  Register_11 = 74HC595 SMD [package="SO16 [SMD]"]
  J262 = double row female pin header, 8 pins [form="♀ (female)"]
  J263 = double row female pin header, 8 pins [form="♀ (female)"]
  Register_12 = 74HC595 SMD [package="SO16 [SMD]"]
  Register_13 = 74HC595 SMD [package="SO16 [SMD]"]
  J264 = double row female pin header, 8 pins [form="♀ (female)"]
  J265 = double row female pin header, 8 pins [form="♀ (female)"]
  J266 = double row female pin header, 8 pins [form="♀ (female)"]
  J267 = double row female pin header, 8 pins [form="♀ (female)"]
  Register_14 = 74HC595 SMD [package="SO16 [SMD]"]
  Register_15 = 74HC595 SMD [package="SO16 [SMD]"]
  Register_16 = 74HC595 SMD [package="SO16 [SMD]"]
  Register_17 = 74HC595 SMD [package="SO16 [SMD]"]
  J268 = double row female pin header, 8 pins [form="♀ (female)"]
  J269 = double row female pin header, 8 pins [form="♀ (female)"]
  J270 = double row female pin header, 8 pins [form="♀ (female)"]
  J271 = double row female pin header, 8 pins [form="♀ (female)"]
  J272 = double row female pin header, 8 pins [form="♀ (female)"]
  J273 = double row female pin header, 8 pins [form="♀ (female)"]
  J274 = double row female pin header, 8 pins [form="♀ (female)"]
  J275 = double row female pin header, 8 pins [form="♀ (female)"]
  Register_18 = 74HC595 SMD [package="SO16 [SMD]"]
  Register_19 = 74HC595 SMD [package="SO16 [SMD]"]
  Register_20 = 74HC595 SMD [package="SO16 [SMD]"]
  Register_21 = 74HC595 SMD [package="SO16 [SMD]"]
  Register_22 = 74HC595 SMD [package="SO16 [SMD]"]
  Register_23 = 74HC595 SMD [package="SO16 [SMD]"]
  Register_24 = 74HC595 SMD [package="SO16 [SMD]"]
  Register_25 = 74HC595 SMD [package="SO16 [SMD]"]
  J276 = double row female pin header, 8 pins [form="♀ (female)"]
  J277 = double row female pin header, 8 pins [form="♀ (female)"]
  J278 = double row female pin header, 8 pins [form="♀ (female)"]
  J279 = double row female pin header, 8 pins [form="♀ (female)"]
  J280 = double row female pin header, 8 pins [form="♀ (female)"]
  J281 = double row female pin header, 8 pins [form="♀ (female)"]
  J282 = double row female pin header, 8 pins [form="♀ (female)"]
  J283 = double row female pin header, 8 pins [form="♀ (female)"]
  J284 = double row female pin header, 8 pins [form="♀ (female)"]
  J285 = double row female pin header, 8 pins [form="♀ (female)"]
  J286 = double row female pin header, 8 pins [form="♀ (female)"]
  J287 = double row female pin header, 8 pins [form="♀ (female)"]
  J288 = double row female pin header, 8 pins [form="♀ (female)"]
  J289 = double row female pin header, 8 pins [form="♀ (female)"]
  J290 = double row female pin header, 8 pins [form="♀ (female)"]
  J291 = double row female pin header, 8 pins [form="♀ (female)"]
  Register_26 = 74HC595 SMD [package="SO16 [SMD]"]
  Register_27 = 74HC595 SMD [package="SO16 [SMD]"]
  Register_28 = 74HC595 SMD [package="SO16 [SMD]"]
  Register_29 = 74HC595 SMD [package="SO16 [SMD]"]
  Register_30 = 74HC595 SMD [package="SO16 [SMD]"]
  Register_31 = 74HC595 SMD [package="SO16 [SMD]"]
  Register_32 = 74HC595 SMD [package="SO16 [SMD]"]
  Register_33 = 74HC595 SMD [package="SO16 [SMD]"]
  Register_34 = 74HC595 SMD [package="SO16 [SMD]"]
  Register_35 = 74HC595 SMD [package="SO16 [SMD]"]
  Register_36 = 74HC595 SMD [package="SO16 [SMD]"]
  Register_37 = 74HC595 SMD [package="SO16 [SMD]"]
  Register_38 = 74HC595 SMD [package="SO16 [SMD]"]
  Register_39 = 74HC595 SMD [package="SO16 [SMD]"]
  Register_40 = 74HC595 SMD [package="SO16 [SMD]"]
  Register_41 = 74HC595 SMD [package="SO16 [SMD]"]
  J292 = double row female pin header, 8 pins [form="♀ (female)"]
  J293 = double row female pin header, 8 pins [form="♀ (female)"]
  J294 = double row female pin header, 8 pins [form="♀ (female)"]
  J295 = double row female pin header, 8 pins [form="♀ (female)"]
  J296 = double row female pin header, 8 pins [form="♀ (female)"]
  J297 = double row female pin header, 8 pins [form="♀ (female)"]
  J298 = double row female pin header, 8 pins [form="♀ (female)"]
  J299 = double row female pin header, 8 pins [form="♀ (female)"]
  J300 = double row female pin header, 8 pins [form="♀ (female)"]
  J301 = double row female pin header, 8 pins [form="♀ (female)"]
  J302 = double row female pin header, 8 pins [form="♀ (female)"]
  J303 = double row female pin header, 8 pins [form="♀ (female)"]
  J304 = double row female pin header, 8 pins [form="♀ (female)"]
  J305 = double row female pin header, 8 pins [form="♀ (female)"]
  J306 = double row female pin header, 8 pins [form="♀ (female)"]
  J307 = double row female pin header, 8 pins [form="♀ (female)"]
  Register_42 = 74HC595 SMD [package="SO16 [SMD]"]
  Register_43 = 74HC595 SMD [package="SO16 [SMD]"]
  Register_44 = 74HC595 SMD [package="SO16 [SMD]"]
  Register_45 = 74HC595 SMD [package="SO16 [SMD]"]
  Register_46 = 74HC595 SMD [package="SO16 [SMD]"]
  Register_47 = 74HC595 SMD [package="SO16 [SMD]"]
  Register_48 = 74HC595 SMD [package="SO16 [SMD]"]
  Register_49 = 74HC595 SMD [package="SO16 [SMD]"]
  Register_50 = 74HC595 SMD [package="SO16 [SMD]"]
  Register_51 = 74HC595 SMD [package="SO16 [SMD]"]
  Register_52 = 74HC595 SMD [package="SO16 [SMD]"]
  Register_53 = 74HC595 SMD [package="SO16 [SMD]"]
  Register_54 = 74HC595 SMD [package="SO16 [SMD]"]
  Register_55 = 74HC595 SMD [package="SO16 [SMD]"]
  Register_56 = 74HC595 SMD [package="SO16 [SMD]"]
  Register_57 = 74HC595 SMD [package="SO16 [SMD]"]
  J308 = double row female pin header, 8 pins [form="♀ (female)"]
  J309 = double row female pin header, 8 pins [form="♀ (female)"]
  J310 = double row female pin header, 8 pins [form="♀ (female)"]
  J311 = double row female pin header, 8 pins [form="♀ (female)"]
  J312 = double row female pin header, 8 pins [form="♀ (female)"]
  J313 = double row female pin header, 8 pins [form="♀ (female)"]
  J314 = double row female pin header, 8 pins [form="♀ (female)"]
  J315 = double row female pin header, 8 pins [form="♀ (female)"]
  J316 = double row female pin header, 8 pins [form="♀ (female)"]
  J317 = double row female pin header, 8 pins [form="♀ (female)"]
  J318 = double row female pin header, 8 pins [form="♀ (female)"]
  J319 = double row female pin header, 8 pins [form="♀ (female)"]
  J320 = double row female pin header, 8 pins [form="♀ (female)"]
  J321 = double row female pin header, 8 pins [form="♀ (female)"]
  J322 = double row female pin header, 8 pins [form="♀ (female)"]
  J323 = double row female pin header, 8 pins [form="♀ (female)"]
  Register_58 = 74HC595 SMD [package="SO16 [SMD]"]
  Register_59 = 74HC595 SMD [package="SO16 [SMD]"]
  Register_60 = 74HC595 SMD [package="SO16 [SMD]"]
  Register_61 = 74HC595 SMD [package="SO16 [SMD]"]
  Register_62 = 74HC595 SMD [package="SO16 [SMD]"]
  Register_63 = 74HC595 SMD [package="SO16 [SMD]"]
  Register_64 = 74HC595 SMD [package="SO16 [SMD]"]
  Register_65 = 74HC595 SMD [package="SO16 [SMD]"]
  Register_66 = 74HC595 SMD [package="SO16 [SMD]"]
  Register_67 = 74HC595 SMD [package="SO16 [SMD]"]
  Register_68 = 74HC595 SMD [package="SO16 [SMD]"]
  Register_69 = 74HC595 SMD [package="SO16 [SMD]"]
  Register_70 = 74HC595 SMD [package="SO16 [SMD]"]
  Register_71 = 74HC595 SMD [package="SO16 [SMD]"]
  Register_72 = 74HC595 SMD [package="SO16 [SMD]"]
  Register_73 = 74HC595 SMD [package="SO16 [SMD]"]
  J325 = STARBOARD_GND [package=starboard_ground]  # not connected

nets:
  N1: ATmega_2560_16au.(OC0B)PG5, Register_40.DS
  N2: ATmega_2560_16au.(RXD0_PCIN8)PE0, R3.Pin_0, Register_10.SH_CP, Register_11.SH_CP, Register_12.SH_CP, Register_13.SH_CP, Register_14.SH_CP, Register_15.SH_CP, Register_16.SH_CP, Register_17.SH_CP, Register_18.ST_CP, Register_19.ST_CP, Register_20.ST_CP, Register_21.ST_CP, Register_22.ST_CP, Register_23.ST_CP, Register_24.ST_CP, Register_25.ST_CP, Register_26.ST_CP, Register_27.ST_CP, Register_28.ST_CP, Register_29.ST_CP, Register_30.ST_CP, Register_31.ST_CP, Register_32.ST_CP, Register_33.ST_CP, Register_34.ST_CP, Register_35.ST_CP, Register_36.ST_CP, Register_37.ST_CP, Register_38.ST_CP, Register_39.ST_CP, Register_40.ST_CP, Register_41.ST_CP, Register_42.ST_CP, Register_43.ST_CP, Register_44.ST_CP, Register_45.ST_CP, Register_46.ST_CP, Register_47.ST_CP, Register_48.ST_CP, Register_49.ST_CP, Register_50.ST_CP, Register_51.ST_CP, Register_52.ST_CP, Register_53.ST_CP, Register_54.ST_CP, Register_55.ST_CP, Register_56.ST_CP, Register_57.ST_CP, Register_58.ST_CP, Register_59.ST_CP, Register_60.ST_CP, Register_61.ST_CP, Register_62.ST_CP, Register_63.ST_CP, Register_64.ST_CP, Register_65.ST_CP, Register_66.ST_CP, Register_67.ST_CP, Register_68.ST_CP, Register_69.ST_CP, Register_70.ST_CP, Register_71.ST_CP, Register_72.ST_CP, Register_73.ST_CP
  N3: ATmega_2560_16au.(TXD0)PE1, R2.Pin_0, Register_10.ST_CP, Register_11.ST_CP, Register_12.ST_CP, Register_13.ST_CP, Register_14.ST_CP, Register_15.ST_CP, Register_16.ST_CP, Register_17.ST_CP, Register_18.SH_CP, Register_19.SH_CP, Register_20.SH_CP, Register_21.SH_CP, Register_22.SH_CP, Register_23.SH_CP, Register_24.SH_CP, Register_25.SH_CP, Register_26.SH_CP, Register_27.SH_CP, Register_28.SH_CP, Register_29.SH_CP, Register_30.SH_CP, Register_31.SH_CP, Register_32.SH_CP, Register_33.SH_CP, Register_34.SH_CP, Register_35.SH_CP, Register_36.SH_CP, Register_37.SH_CP, Register_38.SH_CP, Register_39.SH_CP, Register_40.SH_CP, Register_41.SH_CP, Register_42.SH_CP, Register_43.SH_CP, Register_44.SH_CP, Register_45.SH_CP, Register_46.SH_CP, Register_47.SH_CP, Register_48.SH_CP, Register_49.SH_CP, Register_50.SH_CP, Register_51.SH_CP, Register_52.SH_CP, Register_53.SH_CP, Register_54.SH_CP, Register_55.SH_CP, Register_56.SH_CP, Register_57.SH_CP, Register_58.SH_CP, Register_59.SH_CP, Register_60.SH_CP, Register_61.SH_CP, Register_62.SH_CP, Register_63.SH_CP, Register_64.SH_CP, Register_65.SH_CP, Register_66.SH_CP, Register_67.SH_CP, Register_68.SH_CP, Register_69.SH_CP, Register_70.SH_CP, Register_71.SH_CP, Register_72.SH_CP, Register_73.SH_CP
  N4: ATmega_2560_16au.(OC3A_AIN1)PE3, Register_41.DS
  N5: ATmega_2560_16au.(OC3B_INT4)PE4, Register_10.DS
  N6: ATmega_2560_16au.(OC3C_INT5)PE5, Register_25.DS
  VCC: ATmega_2560_16au.VCC, ATmega_2560_16au.VCC1, ATmega_2560_16au.VCC2, ATmega_2560_16au.VCC3, ATmega_2560_16au.AVCC, ICSP.2, ICSP_U2.2, R1.Pin_0, D1.cathode, C2.2, R6.Pin_1, R7.Pin_1, R13.Pin_1, C11.1, C12.1, C13.1, R16.Pin_0, R15.Pin_0, D2.cathode, R17.Pin_0, U7.VCC, U7.AVCC
  GND: ATmega_2560_16au.GND, ATmega_2560_16au.GND1, ATmega_2560_16au.GND2, ATmega_2560_16au.GND3, ATmega_2560_16au.AGND, ICSP.6, ICSP_U2.6, C2.1, C3.1, U2.IN, U2.GND, U2.EN, VIN_GND.pin1, R9.Pin_1, C4.2, U3.G$1_GND, U3.G$1_+V, C5.1, C5.2, U4.S, C6.1, R10.Pin_0, C8.1, C9.1, LED3.cathode, LED4.cathode, U6.2, C10.2, C11.2, C12.2, C13.2, C14.2, U7.GND, U7.Pad_GND, RESET.Pin_3, RESET.Pin_4, Register_10.GND, Register_10.OE, Register_11.GND, Register_11.OE, Register_12.GND, Register_12.OE, Register_13.GND, Register_13.OE, Register_14.GND, Register_14.OE, Register_15.GND, Register_15.OE, Register_16.GND, Register_16.OE, Register_17.GND, Register_17.OE, Register_18.GND, Register_18.OE, Register_19.GND, Register_19.OE, Register_20.GND, Register_20.OE, Register_21.GND, Register_21.OE, Register_22.GND, Register_22.OE, Register_23.GND, Register_23.OE, Register_24.GND, Register_24.OE, Register_25.GND, Register_25.OE, Register_26.GND, Register_26.OE, Register_27.GND, Register_27.OE, Register_28.GND, Register_28.OE, Register_29.GND, Register_29.OE, Register_30.GND, Register_30.OE, Register_31.GND, Register_31.OE, Register_32.GND, Register_32.OE, Register_33.GND, Register_33.OE, Register_34.GND, Register_34.OE, Register_35.GND, Register_35.OE, Register_36.GND, Register_36.OE, Register_37.GND, Register_37.OE, Register_38.GND, Register_38.OE, Register_39.GND, Register_39.OE, Register_40.GND, Register_40.OE, Register_41.GND, Register_41.OE, Register_42.GND, Register_42.OE, Register_43.GND, Register_43.OE, Register_44.GND, Register_44.OE, Register_45.GND, Register_45.OE, Register_46.GND, Register_46.OE, Register_47.GND, Register_47.OE, Register_48.GND, Register_48.OE, Register_49.GND, Register_49.OE, Register_50.GND, Register_50.OE, Register_51.GND, Register_51.OE, Register_52.GND, Register_52.OE, Register_53.GND, Register_53.OE, Register_54.GND, Register_54.OE, Register_55.GND, Register_55.OE, Register_56.GND, Register_56.OE, Register_57.GND, Register_57.OE, Register_58.GND, Register_58.OE, Register_59.GND, Register_59.OE, Register_60.GND, Register_60.OE, Register_61.GND, Register_61.OE, Register_62.GND, Register_62.OE, Register_63.GND, Register_63.OE, Register_64.GND, Register_64.OE, Register_65.GND, Register_65.OE, Register_66.GND, Register_66.OE, Register_67.GND, Register_67.OE, Register_68.GND, Register_68.OE, Register_69.GND, Register_69.OE, Register_70.GND, Register_70.OE, Register_71.GND, Register_71.OE, Register_72.GND, Register_72.OE, Register_73.GND, Register_73.OE
  N7: ATmega_2560_16au.PH0(RXD2), J257.pin4, J257.pin12
  N8: ATmega_2560_16au.PH1(TXD2), J257.pin5, J257.pin13
  N9: ATmega_2560_16au.PH3(OC4A), Register_56.DS
  N10: ATmega_2560_16au.PH4(OC4B), Register_57.DS
  N11: ATmega_2560_16au.PH5(OC4C), Register_72.DS
  N12: ATmega_2560_16au.PH6(OC2B), Register_73.DS
  N13: ATmega_2560_16au.(SS_PCINT0)PB0, J257.pin14
  N14: ATmega_2560_16au.(SCK_PCINT1)PB1, ICSP.3, J257.pin15
  N15: ATmega_2560_16au.(MOSI_PCINT2)PB2, ICSP.4, J257.pin16
  N16: ATmega_2560_16au.(MISO_PCINT3)PB3, ICSP.1, J257.pin17
  N17: ATmega_2560_16au.(OC2A_PCINT4)PB4, J257.pin18
  N18: ATmega_2560_16au.(OC1A_PCINT5)PB5, J257.pin19
  N19: ATmega_2560_16au.(OC1B_PCINT6)PB6, J257.pin20
  N20: ATmega_2560_16au.(OC0A_OC1C_PCINT7)PB7, U5.G$1_+IN1, J48.pin1
  N21: ATmega_2560_16au.RESET, ICSP.5, RESET-EN.pin2, D2.anode, R17.Pin_1, C14.1, RESET.Pin_2
  N22: ATmega_2560_16au.XTAL2, R14.Pin_0, U6.1
  N23: ATmega_2560_16au.XTAL1, R14.Pin_1, U6.3
  N24: ATmega_2560_16au.PL0(ICP4), J48.pin7
  N25: ATmega_2560_16au.PL1(ICP5), J48.pin6
  N26: ATmega_2560_16au.PL2(T5), J48.pin5
  N27: ATmega_2560_16au.PL3(OC5A), J48.pin4
  N28: ATmega_2560_16au.PL4(OC5B), J48.pin3
  N29: ATmega_2560_16au.PL5(OC5C), J48.pin2
  N30: ATmega_2560_16au.PL6, J48.pin14
  N31: ATmega_2560_16au.PL7, J48.pin13
  N32: ATmega_2560_16au.(SCL_INT0)PD0, R15.Pin_1, J48.pin12
  N33: ATmega_2560_16au.(SDA_INT1)PD1, R16.Pin_1, J48.pin11
  N34: ATmega_2560_16au.(RXD1_INT2)PD2, J48.pin10
  N35: ATmega_2560_16au.(TXD1_INT3)PD3, J48.pin9
  N36: ATmega_2560_16au.(T0)PD7, J48.pin8
  N37: ATmega_2560_16au.(WR)PG0, J257.pin30
  N38: ATmega_2560_16au.(RD)PG1, J257.pin29
  N39: ATmega_2560_16au.(A8)PC0, J257.pin28
  N40: ATmega_2560_16au.(A9)PC1, J257.pin27
  N41: ATmega_2560_16au.(A10)PC2, J257.pin26
  N42: ATmega_2560_16au.(A11)PC3, J257.pin25
  N43: ATmega_2560_16au.(A12)PC4, J257.pin24
  N44: ATmega_2560_16au.(A13)PC5, J257.pin23
  N45: ATmega_2560_16au.(A14)PC6, J257.pin22
  N46: ATmega_2560_16au.(A15)PC7, J257.pin21
  N47: ATmega_2560_16au.(ALE)PG2, J257.pin11
  N48: ATmega_2560_16au.(AD7)PA7, J257.pin10
  N49: ATmega_2560_16au.(AD6)PA6, J257.pin9
  N50: ATmega_2560_16au.(AD5)PA5, J257.pin8
  N51: ATmega_2560_16au.(AD4)PA4, J257.pin7
  N52: ATmega_2560_16au.(AD3)PA3, J257.pin6
  N53: ATmega_2560_16au.(AD2)PA2, J257.pin3
  N54: ATmega_2560_16au.(AD1)PA1, J257.pin2
  N55: ATmega_2560_16au.(AD0)PA0, J257.pin1
  N56: ATmega_2560_16au.PK7(ADC15_PCINT23), J256.pin16
  N57: ATmega_2560_16au.PK6(ADC14_PCINT22), J256.pin15
  N58: ATmega_2560_16au.PK5(ADC13_PCINT21), J256.pin14
  N59: ATmega_2560_16au.PK4(ADC12_PCINT20), J256.pin13
  N60: ATmega_2560_16au.PK3(ADC11_PCINT19), J256.pin12
  N61: ATmega_2560_16au.PK2(ADC10_PCINT18), J256.pin11
  N62: ATmega_2560_16au.PK1(ADC9_PCINT17), J256.pin10
  N63: ATmega_2560_16au.PK0(ADC8_PCINT16), J256.pin9
  N64: ATmega_2560_16au.(ADC7_TDI)PF7, J256.pin8
  N65: ATmega_2560_16au.(ADC6_TDO)PF6, J256.pin7
  N66: ATmega_2560_16au.(ADC5_TMS)PF5, J256.pin6
  N67: ATmega_2560_16au.(ADC4_TCK)PF4, J256.pin5
  N68: ATmega_2560_16au.(ADC3)PF3, J256.pin4
  N69: ATmega_2560_16au.(ADC2)PF2, J256.pin3
  N70: ATmega_2560_16au.(ADC1)PF1, J256.pin2
  N71: ATmega_2560_16au.(ADC0)PF0, J256.pin1
  N72: ATmega_2560_16au.AREF, C10.1
  N73: ICSP_U2.1, U7.PB3
  N74: ICSP_U2.3, U7.PB1
  N75: ICSP_U2.4, U7.PB2
  N76: ICSP_U2.5, R1.Pin_1, D1.anode, RESET-EN.pin1, C7.2, U7.Reset
  N77: R2.Pin_1, U7.PD2
  N78: R3.Pin_1, U7.PD3
  N79: USB_b.P$1, USB_b.P$2, Z1.2, Z2.2, L1.2
  N80: USB_b.D+, Z2.1, R4.Pin_1
  N81: USB_b.D-, Z1.1, R5.Pin_1
  N82: USB_b.GND, C1.2, L1.1, U7.UGND
  N83: USB_b.VBUS, F1.2
  N84: C1.1, U7.UCAP
  N85: F1.1, C3.2, U4.D, U7.UVCC
  N86: LED1.cathode, U7.PD5
  N87: LED1.anode, R6.Pin_0
  N88: LED2.cathode, U7.PD4
  N89: LED2.anode, R7.Pin_0
  N90: U2.OUT, U3.G$2_-IN2, C6.2
  N91: VIN_GND.pin2, R8.Pin_0
  N92: R8.Pin_1, R9.Pin_0, C4.1, U3.G$2_+IN2
  N93: R4.Pin_0, U7.D+
  N94: R5.Pin_0, U7.D-
  N95: U3.G$2_OUT2, U4.G
  N96: C7.1, R10.Pin_1, U7.PD7
  N97: XTAL1.pin_0, R11.Pin_0, C8.2, U7.XTAL1
  N98: XTAL1.pin_1, R11.Pin_1, C9.2, U7.XTAL2
  N99: U5.G$1_OUT1, U5.G$1_-IN1, R12.Pin_1
  N100: R12.Pin_0, LED3.anode
  N101: LED4.anode, R13.Pin_0
  N102: U7.PB4, pin_1_pin_2.pin3
  N103: U7.PB5, pin_1_pin_2.pin2
  N104: U7.PB6, pin_1_pin_2.pin4
  N105: U7.PB7, pin_1_pin_2.pin1
  N106: J260.pin1, Register_10.Q3
  N107: J260.pin2, Register_10.Q2
  N108: J260.pin3, Register_10.Q1
  N109: J260.pin4, Register_10.Q0
  N110: J260.pin5, Register_10.Q4
  N111: J260.pin6, Register_10.Q5
  N112: J260.pin7, Register_10.Q6
  N113: J260.pin8, Register_10.Q7
  N114: Register_10.Q7', Register_11.DS
  N115: Register_10.MR, Register_10.VCC
  N116: J261.pin1, Register_11.Q3
  N117: J261.pin2, Register_11.Q2
  N118: J261.pin3, Register_11.Q1
  N119: J261.pin4, Register_11.Q0
  N120: J261.pin5, Register_11.Q4
  N121: J261.pin6, Register_11.Q5
  N122: J261.pin7, Register_11.Q6
  N123: J261.pin8, Register_11.Q7
  N124: Register_11.Q7', Register_12.DS
  N125: Register_11.MR, Register_11.VCC
  N126: J262.pin1, Register_12.Q3
  N127: J262.pin2, Register_12.Q2
  N128: J262.pin3, Register_12.Q1
  N129: J262.pin4, Register_12.Q0
  N130: J262.pin5, Register_12.Q4
  N131: J262.pin6, Register_12.Q5
  N132: J262.pin7, Register_12.Q6
  N133: J262.pin8, Register_12.Q7
  N134: J263.pin1, Register_13.Q3
  N135: J263.pin2, Register_13.Q2
  N136: J263.pin3, Register_13.Q1
  N137: J263.pin4, Register_13.Q0
  N138: J263.pin5, Register_13.Q4
  N139: J263.pin6, Register_13.Q5
  N140: J263.pin7, Register_13.Q6
  N141: J263.pin8, Register_13.Q7
  N142: Register_12.Q7', Register_13.DS
  N143: Register_12.MR, Register_12.VCC
  N144: Register_13.Q7', Register_14.DS
  N145: Register_13.MR, Register_13.VCC
  N146: J264.pin1, Register_14.Q3
  N147: J264.pin2, Register_14.Q2
  N148: J264.pin3, Register_14.Q1
  N149: J264.pin4, Register_14.Q0
  N150: J264.pin5, Register_14.Q4
  N151: J264.pin6, Register_14.Q5
  N152: J264.pin7, Register_14.Q6
  N153: J264.pin8, Register_14.Q7
  N154: J265.pin1, Register_15.Q3
  N155: J265.pin2, Register_15.Q2
  N156: J265.pin3, Register_15.Q1
  N157: J265.pin4, Register_15.Q0
  N158: J265.pin5, Register_15.Q4
  N159: J265.pin6, Register_15.Q5
  N160: J265.pin7, Register_15.Q6
  N161: J265.pin8, Register_15.Q7
  N162: J266.pin1, Register_16.Q3
  N163: J266.pin2, Register_16.Q2
  N164: J266.pin3, Register_16.Q1
  N165: J266.pin4, Register_16.Q0
  N166: J266.pin5, Register_16.Q4
  N167: J266.pin6, Register_16.Q5
  N168: J266.pin7, Register_16.Q6
  N169: J266.pin8, Register_16.Q7
  N170: J267.pin1, Register_17.Q3
  N171: J267.pin2, Register_17.Q2
  N172: J267.pin3, Register_17.Q1
  N173: J267.pin4, Register_17.Q0
  N174: J267.pin5, Register_17.Q4
  N175: J267.pin6, Register_17.Q5
  N176: J267.pin7, Register_17.Q6
  N177: J267.pin8, Register_17.Q7
  N178: Register_14.Q7', Register_15.DS
  N179: Register_14.MR, Register_14.VCC
  N180: Register_15.Q7', Register_17.DS
  N181: Register_15.MR, Register_15.VCC
  N182: Register_16.MR, Register_16.VCC
  N183: Register_16.DS, Register_17.Q7'
  N184: Register_17.MR, Register_17.VCC
  N185: J268.pin1, Register_18.Q3
  N186: J268.pin2, Register_18.Q2
  N187: J268.pin3, Register_18.Q1
  N188: J268.pin4, Register_18.Q0
  N189: J268.pin5, Register_18.Q4
  N190: J268.pin6, Register_18.Q5
  N191: J268.pin7, Register_18.Q6
  N192: J268.pin8, Register_18.Q7
  N193: J269.pin1, Register_19.Q3
  N194: J269.pin2, Register_19.Q2
  N195: J269.pin3, Register_19.Q1
  N196: J269.pin4, Register_19.Q0
  N197: J269.pin5, Register_19.Q4
  N198: J269.pin6, Register_19.Q5
  N199: J269.pin7, Register_19.Q6
  N200: J269.pin8, Register_19.Q7
  N201: J270.pin1, Register_20.Q3
  N202: J270.pin2, Register_20.Q2
  N203: J270.pin3, Register_20.Q1
  N204: J270.pin4, Register_20.Q0
  N205: J270.pin5, Register_20.Q4
  N206: J270.pin6, Register_20.Q5
  N207: J270.pin7, Register_20.Q6
  N208: J270.pin8, Register_20.Q7
  N209: J271.pin1, Register_21.Q3
  N210: J271.pin2, Register_21.Q2
  N211: J271.pin3, Register_21.Q1
  N212: J271.pin4, Register_21.Q0
  N213: J271.pin5, Register_21.Q4
  N214: J271.pin6, Register_21.Q5
  N215: J271.pin7, Register_21.Q6
  N216: J271.pin8, Register_21.Q7
  N217: J272.pin1, Register_22.Q3
  N218: J272.pin2, Register_22.Q2
  N219: J272.pin3, Register_22.Q1
  N220: J272.pin4, Register_22.Q0
  N221: J272.pin5, Register_22.Q4
  N222: J272.pin6, Register_22.Q5
  N223: J272.pin7, Register_22.Q6
  N224: J272.pin8, Register_22.Q7
  N225: J273.pin1, Register_23.Q3
  N226: J273.pin2, Register_23.Q2
  N227: J273.pin3, Register_23.Q1
  N228: J273.pin4, Register_23.Q0
  N229: J273.pin5, Register_23.Q4
  N230: J273.pin6, Register_23.Q5
  N231: J273.pin7, Register_23.Q6
  N232: J273.pin8, Register_23.Q7
  N233: J274.pin1, Register_24.Q3
  N234: J274.pin2, Register_24.Q2
  N235: J274.pin3, Register_24.Q1
  N236: J274.pin4, Register_24.Q0
  N237: J274.pin5, Register_24.Q4
  N238: J274.pin6, Register_24.Q5
  N239: J274.pin7, Register_24.Q6
  N240: J274.pin8, Register_24.Q7
  N241: J275.pin1, Register_25.Q3
  N242: J275.pin2, Register_25.Q2
  N243: J275.pin3, Register_25.Q1
  N244: J275.pin4, Register_25.Q0
  N245: J275.pin5, Register_25.Q4
  N246: J275.pin6, Register_25.Q5
  N247: J275.pin7, Register_25.Q6
  N248: J275.pin8, Register_25.Q7
  N249: Register_18.Q7', Register_19.DS
  N250: Register_18.MR, Register_18.VCC
  N251: Register_18.DS, Register_20.Q7'
  N252: Register_19.MR, Register_19.VCC
  N253: Register_20.MR, Register_20.VCC
  N254: Register_20.DS, Register_21.Q7'
  N255: Register_21.MR, Register_21.VCC
  N256: Register_21.DS, Register_22.Q7'
  N257: Register_22.MR, Register_22.VCC
  N258: Register_22.DS, Register_23.Q7'
  N259: Register_23.MR, Register_23.VCC
  N260: Register_23.DS, Register_24.Q7'
  N261: Register_24.MR, Register_24.VCC
  N262: Register_24.DS, Register_25.Q7'
  N263: Register_25.MR, Register_25.VCC
  N264: J276.pin1, Register_26.Q3
  N265: J276.pin2, Register_26.Q2
  N266: J276.pin3, Register_26.Q1
  N267: J276.pin4, Register_26.Q0
  N268: J276.pin5, Register_26.Q4
  N269: J276.pin6, Register_26.Q5
  N270: J276.pin7, Register_26.Q6
  N271: J276.pin8, Register_26.Q7
  N272: J277.pin1, Register_27.Q3
  N273: J277.pin2, Register_27.Q2
  N274: J277.pin3, Register_27.Q1
  N275: J277.pin4, Register_27.Q0
  N276: J277.pin5, Register_27.Q4
  N277: J277.pin6, Register_27.Q5
  N278: J277.pin7, Register_27.Q6
  N279: J277.pin8, Register_27.Q7
  N280: J278.pin1, Register_28.Q3
  N281: J278.pin2, Register_28.Q2
  N282: J278.pin3, Register_28.Q1
  N283: J278.pin4, Register_28.Q0
  N284: J278.pin5, Register_28.Q4
  N285: J278.pin6, Register_28.Q5
  N286: J278.pin7, Register_28.Q6
  N287: J278.pin8, Register_28.Q7
  N288: J279.pin1, Register_29.Q3
  N289: J279.pin2, Register_29.Q2
  N290: J279.pin3, Register_29.Q1
  N291: J279.pin4, Register_29.Q0
  N292: J279.pin5, Register_29.Q4
  N293: J279.pin6, Register_29.Q5
  N294: J279.pin7, Register_29.Q6
  N295: J279.pin8, Register_29.Q7
  N296: J280.pin1, Register_30.Q3
  N297: J280.pin2, Register_30.Q2
  N298: J280.pin3, Register_30.Q1
  N299: J280.pin4, Register_30.Q0
  N300: J280.pin5, Register_30.Q4
  N301: J280.pin6, Register_30.Q5
  N302: J280.pin7, Register_30.Q6
  N303: J280.pin8, Register_30.Q7
  N304: J281.pin1, Register_31.Q3
  N305: J281.pin2, Register_31.Q2
  N306: J281.pin3, Register_31.Q1
  N307: J281.pin4, Register_31.Q0
  N308: J281.pin5, Register_31.Q4
  N309: J281.pin6, Register_31.Q5
  N310: J281.pin7, Register_31.Q6
  N311: J281.pin8, Register_31.Q7
  N312: J282.pin1, Register_32.Q3
  N313: J282.pin2, Register_32.Q2
  N314: J282.pin3, Register_32.Q1
  N315: J282.pin4, Register_32.Q0
  N316: J282.pin5, Register_32.Q4
  N317: J282.pin6, Register_32.Q5
  N318: J282.pin7, Register_32.Q6
  N319: J282.pin8, Register_32.Q7
  N320: J283.pin1, Register_33.Q3
  N321: J283.pin2, Register_33.Q2
  N322: J283.pin3, Register_33.Q1
  N323: J283.pin4, Register_33.Q0
  N324: J283.pin5, Register_33.Q4
  N325: J283.pin6, Register_33.Q5
  N326: J283.pin7, Register_33.Q6
  N327: J283.pin8, Register_33.Q7
  N328: J284.pin1, Register_34.Q3
  N329: J284.pin2, Register_34.Q2
  N330: J284.pin3, Register_34.Q1
  N331: J284.pin4, Register_34.Q0
  N332: J284.pin5, Register_34.Q4
  N333: J284.pin6, Register_34.Q5
  N334: J284.pin7, Register_34.Q6
  N335: J284.pin8, Register_34.Q7
  N336: J285.pin1, Register_35.Q3
  N337: J285.pin2, Register_35.Q2
  N338: J285.pin3, Register_35.Q1
  N339: J285.pin4, Register_35.Q0
  N340: J285.pin5, Register_35.Q4
  N341: J285.pin6, Register_35.Q5
  N342: J285.pin7, Register_35.Q6
  N343: J285.pin8, Register_35.Q7
  N344: J286.pin1, Register_36.Q3
  N345: J286.pin2, Register_36.Q2
  N346: J286.pin3, Register_36.Q1
  N347: J286.pin4, Register_36.Q0
  N348: J286.pin5, Register_36.Q4
  N349: J286.pin6, Register_36.Q5
  N350: J286.pin7, Register_36.Q6
  N351: J286.pin8, Register_36.Q7
  N352: J287.pin1, Register_37.Q3
  N353: J287.pin2, Register_37.Q2
  N354: J287.pin3, Register_37.Q1
  N355: J287.pin4, Register_37.Q0
  N356: J287.pin5, Register_37.Q4
  N357: J287.pin6, Register_37.Q5
  N358: J287.pin7, Register_37.Q6
  N359: J287.pin8, Register_37.Q7
  N360: J288.pin1, Register_38.Q3
  N361: J288.pin2, Register_38.Q2
  N362: J288.pin3, Register_38.Q1
  N363: J288.pin4, Register_38.Q0
  N364: J288.pin5, Register_38.Q4
  N365: J288.pin6, Register_38.Q5
  N366: J288.pin7, Register_38.Q6
  N367: J288.pin8, Register_38.Q7
  N368: J289.pin1, Register_39.Q3
  N369: J289.pin2, Register_39.Q2
  N370: J289.pin3, Register_39.Q1
  N371: J289.pin4, Register_39.Q0
  N372: J289.pin5, Register_39.Q4
  N373: J289.pin6, Register_39.Q5
  N374: J289.pin7, Register_39.Q6
  N375: J289.pin8, Register_39.Q7
  N376: J290.pin1, Register_40.Q3
  N377: J290.pin2, Register_40.Q2
  N378: J290.pin3, Register_40.Q1
  N379: J290.pin4, Register_40.Q0
  N380: J290.pin5, Register_40.Q4
  N381: J290.pin6, Register_40.Q5
  N382: J290.pin7, Register_40.Q6
  N383: J290.pin8, Register_40.Q7
  N384: J291.pin1, Register_41.Q3
  N385: J291.pin2, Register_41.Q2
  N386: J291.pin3, Register_41.Q1
  N387: J291.pin4, Register_41.Q0
  N388: J291.pin5, Register_41.Q4
  N389: J291.pin6, Register_41.Q5
  N390: J291.pin7, Register_41.Q6
  N391: J291.pin8, Register_41.Q7
  N392: Register_26.Q7', Register_28.DS
  N393: Register_26.MR, Register_26.VCC
  N394: Register_26.DS, Register_30.Q7'
  N395: Register_27.Q7', Register_29.DS
  N396: Register_27.MR, Register_27.VCC
  N397: Register_27.DS, Register_31.Q7'
  N398: Register_28.MR, Register_28.VCC
  N399: Register_29.MR, Register_29.VCC
  N400: Register_30.MR, Register_30.VCC
  N401: Register_30.DS, Register_32.Q7'
  N402: Register_31.MR, Register_31.VCC
  N403: Register_31.DS, Register_33.Q7'
  N404: Register_32.MR, Register_32.VCC
  N405: Register_32.DS, Register_34.Q7'
  N406: Register_33.MR, Register_33.VCC
  N407: Register_33.DS, Register_35.Q7'
  N408: Register_34.MR, Register_34.VCC
  N409: Register_34.DS, Register_36.Q7'
  N410: Register_35.MR, Register_35.VCC
  N411: Register_35.DS, Register_37.Q7'
  N412: Register_36.MR, Register_36.VCC
  N413: Register_36.DS, Register_38.Q7'
  N414: Register_37.MR, Register_37.VCC
  N415: Register_37.DS, Register_39.Q7'
  N416: Register_38.MR, Register_38.VCC
  N417: Register_38.DS, Register_40.Q7'
  N418: Register_39.MR, Register_39.VCC
  N419: Register_39.DS, Register_41.Q7'
  N420: Register_40.MR, Register_40.VCC
  N421: Register_41.MR, Register_41.VCC
  N422: J292.pin1, Register_43.Q3
  N423: J292.pin2, Register_43.Q2
  N424: J292.pin3, Register_43.Q1
  N425: J292.pin4, Register_43.Q0
  N426: J292.pin5, Register_43.Q4
  N427: J292.pin6, Register_43.Q5
  N428: J292.pin7, Register_43.Q6
  N429: J292.pin8, Register_43.Q7
  N430: J293.pin1, Register_42.Q3
  N431: J293.pin2, Register_42.Q2
  N432: J293.pin3, Register_42.Q1
  N433: J293.pin4, Register_42.Q0
  N434: J293.pin5, Register_42.Q4
  N435: J293.pin6, Register_42.Q5
  N436: J293.pin7, Register_42.Q6
  N437: J293.pin8, Register_42.Q7
  N438: J294.pin1, Register_45.Q3
  N439: J294.pin2, Register_45.Q2
  N440: J294.pin3, Register_45.Q1
  N441: J294.pin4, Register_45.Q0
  N442: J294.pin5, Register_45.Q4
  N443: J294.pin6, Register_45.Q5
  N444: J294.pin7, Register_45.Q6
  N445: J294.pin8, Register_45.Q7
  N446: J295.pin1, Register_44.Q3
  N447: J295.pin2, Register_44.Q2
  N448: J295.pin3, Register_44.Q1
  N449: J295.pin4, Register_44.Q0
  N450: J295.pin5, Register_44.Q4
  N451: J295.pin6, Register_44.Q5
  N452: J295.pin7, Register_44.Q6
  N453: J295.pin8, Register_44.Q7
  N454: J296.pin1, Register_46.Q3
  N455: J296.pin2, Register_46.Q2
  N456: J296.pin3, Register_46.Q1
  N457: J296.pin4, Register_46.Q0
  N458: J296.pin5, Register_46.Q4
  N459: J296.pin6, Register_46.Q5
  N460: J296.pin7, Register_46.Q6
  N461: J296.pin8, Register_46.Q7
  N462: J297.pin1, Register_47.Q3
  N463: J297.pin2, Register_47.Q2
  N464: J297.pin3, Register_47.Q1
  N465: J297.pin4, Register_47.Q0
  N466: J297.pin5, Register_47.Q4
  N467: J297.pin6, Register_47.Q5
  N468: J297.pin7, Register_47.Q6
  N469: J297.pin8, Register_47.Q7
  N470: J298.pin1, Register_49.Q3
  N471: J298.pin2, Register_49.Q2
  N472: J298.pin3, Register_49.Q1
  N473: J298.pin4, Register_49.Q0
  N474: J298.pin5, Register_49.Q4
  N475: J298.pin6, Register_49.Q5
  N476: J298.pin7, Register_49.Q6
  N477: J298.pin8, Register_49.Q7
  N478: J299.pin1, Register_48.Q3
  N479: J299.pin2, Register_48.Q2
  N480: J299.pin3, Register_48.Q1
  N481: J299.pin4, Register_48.Q0
  N482: J299.pin5, Register_48.Q4
  N483: J299.pin6, Register_48.Q5
  N484: J299.pin7, Register_48.Q6
  N485: J299.pin8, Register_48.Q7
  N486: J300.pin1, Register_51.Q3
  N487: J300.pin2, Register_51.Q2
  N488: J300.pin3, Register_51.Q1
  N489: J300.pin4, Register_51.Q0
  N490: J300.pin5, Register_51.Q4
  N491: J300.pin6, Register_51.Q5
  N492: J300.pin7, Register_51.Q6
  N493: J300.pin8, Register_51.Q7
  N494: J301.pin1, Register_50.Q3
  N495: J301.pin2, Register_50.Q2
  N496: J301.pin3, Register_50.Q1
  N497: J301.pin4, Register_50.Q0
  N498: J301.pin5, Register_50.Q4
  N499: J301.pin6, Register_50.Q5
  N500: J301.pin7, Register_50.Q6
  N501: J301.pin8, Register_50.Q7
  N502: J302.pin1, Register_52.Q3
  N503: J302.pin2, Register_52.Q2
  N504: J302.pin3, Register_52.Q1
  N505: J302.pin4, Register_52.Q0
  N506: J302.pin5, Register_52.Q4
  N507: J302.pin6, Register_52.Q5
  N508: J302.pin7, Register_52.Q6
  N509: J302.pin8, Register_52.Q7
  N510: J303.pin1, Register_53.Q3
  N511: J303.pin2, Register_53.Q2
  N512: J303.pin3, Register_53.Q1
  N513: J303.pin4, Register_53.Q0
  N514: J303.pin5, Register_53.Q4
  N515: J303.pin6, Register_53.Q5
  N516: J303.pin7, Register_53.Q6
  N517: J303.pin8, Register_53.Q7
  N518: J304.pin1, Register_55.Q3
  N519: J304.pin2, Register_55.Q2
  N520: J304.pin3, Register_55.Q1
  N521: J304.pin4, Register_55.Q0
  N522: J304.pin5, Register_55.Q4
  N523: J304.pin6, Register_55.Q5
  N524: J304.pin7, Register_55.Q6
  N525: J304.pin8, Register_55.Q7
  N526: J305.pin1, Register_54.Q3
  N527: J305.pin2, Register_54.Q2
  N528: J305.pin3, Register_54.Q1
  N529: J305.pin4, Register_54.Q0
  N530: J305.pin5, Register_54.Q4
  N531: J305.pin6, Register_54.Q5
  N532: J305.pin7, Register_54.Q6
  N533: J305.pin8, Register_54.Q7
  N534: J306.pin1, Register_56.Q3
  N535: J306.pin2, Register_56.Q2
  N536: J306.pin3, Register_56.Q1
  N537: J306.pin4, Register_56.Q0
  N538: J306.pin5, Register_56.Q4
  N539: J306.pin6, Register_56.Q5
  N540: J306.pin7, Register_56.Q6
  N541: J306.pin8, Register_56.Q7
  N542: J307.pin1, Register_57.Q3
  N543: J307.pin2, Register_57.Q2
  N544: J307.pin3, Register_57.Q1
  N545: J307.pin4, Register_57.Q0
  N546: J307.pin5, Register_57.Q4
  N547: J307.pin6, Register_57.Q5
  N548: J307.pin7, Register_57.Q6
  N549: J307.pin8, Register_57.Q7
  N550: Register_42.Q7', Register_45.DS
  N551: Register_42.MR, Register_42.VCC
  N552: Register_42.DS, Register_46.Q7'
  N553: Register_43.Q7', Register_44.DS
  N554: Register_43.MR, Register_43.VCC
  N555: Register_43.DS, Register_47.Q7'
  N556: Register_44.MR, Register_44.VCC
  N557: Register_45.MR, Register_45.VCC
  N558: Register_46.MR, Register_46.VCC
  N559: Register_46.DS, Register_49.Q7'
  N560: Register_47.MR, Register_47.VCC
  N561: Register_47.DS, Register_48.Q7'
  N562: Register_48.MR, Register_48.VCC
  N563: Register_48.DS, Register_51.Q7'
  N564: Register_49.MR, Register_49.VCC
  N565: Register_49.DS, Register_50.Q7'
  N566: Register_50.MR, Register_50.VCC
  N567: Register_50.DS, Register_52.Q7'
  N568: Register_51.MR, Register_51.VCC
  N569: Register_51.DS, Register_53.Q7'
  N570: Register_52.MR, Register_52.VCC
  N571: Register_52.DS, Register_55.Q7'
  N572: Register_53.MR, Register_53.VCC
  N573: Register_53.DS, Register_54.Q7'
  N574: Register_54.MR, Register_54.VCC
  N575: Register_54.DS, Register_57.Q7'
  N576: Register_55.MR, Register_55.VCC
  N577: Register_55.DS, Register_56.Q7'
  N578: Register_56.MR, Register_56.VCC
  N579: Register_57.MR, Register_57.VCC
  N580: J308.pin1, Register_59.Q3
  N581: J308.pin2, Register_59.Q2
  N582: J308.pin3, Register_59.Q1
  N583: J308.pin4, Register_59.Q0
  N584: J308.pin5, Register_59.Q4
  N585: J308.pin6, Register_59.Q5
  N586: J308.pin7, Register_59.Q6
  N587: J308.pin8, Register_59.Q7
  N588: J309.pin1, Register_58.Q3
  N589: J309.pin2, Register_58.Q2
  N590: J309.pin3, Register_58.Q1
  N591: J309.pin4, Register_58.Q0
  N592: J309.pin5, Register_58.Q4
  N593: J309.pin6, Register_58.Q5
  N594: J309.pin7, Register_58.Q6
  N595: J309.pin8, Register_58.Q7
  N596: J310.pin1, Register_61.Q3
  N597: J310.pin2, Register_61.Q2
  N598: J310.pin3, Register_61.Q1
  N599: J310.pin4, Register_61.Q0
  N600: J310.pin5, Register_61.Q4
  N601: J310.pin6, Register_61.Q5
  N602: J310.pin7, Register_61.Q6
  N603: J310.pin8, Register_61.Q7
  N604: J311.pin1, Register_60.Q3
  N605: J311.pin2, Register_60.Q2
  N606: J311.pin3, Register_60.Q1
  N607: J311.pin4, Register_60.Q0
  N608: J311.pin5, Register_60.Q4
  N609: J311.pin6, Register_60.Q5
  N610: J311.pin7, Register_60.Q6
  N611: J311.pin8, Register_60.Q7
  N612: J312.pin1, Register_62.Q3
  N613: J312.pin2, Register_62.Q2
  N614: J312.pin3, Register_62.Q1
  N615: J312.pin4, Register_62.Q0
  N616: J312.pin5, Register_62.Q4
  N617: J312.pin6, Register_62.Q5
  N618: J312.pin7, Register_62.Q6
  N619: J312.pin8, Register_62.Q7
  N620: J313.pin1, Register_63.Q3
  N621: J313.pin2, Register_63.Q2
  N622: J313.pin3, Register_63.Q1
  N623: J313.pin4, Register_63.Q0
  N624: J313.pin5, Register_63.Q4
  N625: J313.pin6, Register_63.Q5
  N626: J313.pin7, Register_63.Q6
  N627: J313.pin8, Register_63.Q7
  N628: J314.pin1, Register_65.Q3
  N629: J314.pin2, Register_65.Q2
  N630: J314.pin3, Register_65.Q1
  N631: J314.pin4, Register_65.Q0
  N632: J314.pin5, Register_65.Q4
  N633: J314.pin6, Register_65.Q5
  N634: J314.pin7, Register_65.Q6
  N635: J314.pin8, Register_65.Q7
  N636: J315.pin1, Register_64.Q3
  N637: J315.pin2, Register_64.Q2
  N638: J315.pin3, Register_64.Q1
  N639: J315.pin4, Register_64.Q0
  N640: J315.pin5, Register_64.Q4
  N641: J315.pin6, Register_64.Q5
  N642: J315.pin7, Register_64.Q6
  N643: J315.pin8, Register_64.Q7
  N644: J316.pin1, Register_67.Q3
  N645: J316.pin2, Register_67.Q2
  N646: J316.pin3, Register_67.Q1
  N647: J316.pin4, Register_67.Q0
  N648: J316.pin5, Register_67.Q4
  N649: J316.pin6, Register_67.Q5
  N650: J316.pin7, Register_67.Q6
  N651: J316.pin8, Register_67.Q7
  N652: J317.pin1, Register_66.Q3
  N653: J317.pin2, Register_66.Q2
  N654: J317.pin3, Register_66.Q1
  N655: J317.pin4, Register_66.Q0
  N656: J317.pin5, Register_66.Q4
  N657: J317.pin6, Register_66.Q5
  N658: J317.pin7, Register_66.Q6
  N659: J317.pin8, Register_66.Q7
  N660: J318.pin1, Register_68.Q3
  N661: J318.pin2, Register_68.Q2
  N662: J318.pin3, Register_68.Q1
  N663: J318.pin4, Register_68.Q0
  N664: J318.pin5, Register_68.Q4
  N665: J318.pin6, Register_68.Q5
  N666: J318.pin7, Register_68.Q6
  N667: J318.pin8, Register_68.Q7
  N668: J319.pin1, Register_69.Q3
  N669: J319.pin2, Register_69.Q2
  N670: J319.pin3, Register_69.Q1
  N671: J319.pin4, Register_69.Q0
  N672: J319.pin5, Register_69.Q4
  N673: J319.pin6, Register_69.Q5
  N674: J319.pin7, Register_69.Q6
  N675: J319.pin8, Register_69.Q7
  N676: J320.pin1, Register_71.Q3
  N677: J320.pin2, Register_71.Q2
  N678: J320.pin3, Register_71.Q1
  N679: J320.pin4, Register_71.Q0
  N680: J320.pin5, Register_71.Q4
  N681: J320.pin6, Register_71.Q5
  N682: J320.pin7, Register_71.Q6
  N683: J320.pin8, Register_71.Q7
  N684: J321.pin1, Register_70.Q3
  N685: J321.pin2, Register_70.Q2
  N686: J321.pin3, Register_70.Q1
  N687: J321.pin4, Register_70.Q0
  N688: J321.pin5, Register_70.Q4
  N689: J321.pin6, Register_70.Q5
  N690: J321.pin7, Register_70.Q6
  N691: J321.pin8, Register_70.Q7
  N692: J322.pin1, Register_72.Q3
  N693: J322.pin2, Register_72.Q2
  N694: J322.pin3, Register_72.Q1
  N695: J322.pin4, Register_72.Q0
  N696: J322.pin5, Register_72.Q4
  N697: J322.pin6, Register_72.Q5
  N698: J322.pin7, Register_72.Q6
  N699: J322.pin8, Register_72.Q7
  N700: J323.pin1, Register_73.Q3
  N701: J323.pin2, Register_73.Q2
  N702: J323.pin3, Register_73.Q1
  N703: J323.pin4, Register_73.Q0
  N704: J323.pin5, Register_73.Q4
  N705: J323.pin6, Register_73.Q5
  N706: J323.pin7, Register_73.Q6
  N707: J323.pin8, Register_73.Q7
  N708: Register_58.Q7', Register_61.DS
  N709: Register_58.MR, Register_58.VCC
  N710: Register_58.DS, Register_62.Q7'
  N711: Register_59.Q7', Register_60.DS
  N712: Register_59.MR, Register_59.VCC
  N713: Register_59.DS, Register_63.Q7'
  N714: Register_60.MR, Register_60.VCC
  N715: Register_61.MR, Register_61.VCC
  N716: Register_62.MR, Register_62.VCC
  N717: Register_62.DS, Register_65.Q7'
  N718: Register_63.MR, Register_63.VCC
  N719: Register_63.DS, Register_64.Q7'
  N720: Register_64.MR, Register_64.VCC
  N721: Register_64.DS, Register_67.Q7'
  N722: Register_65.MR, Register_65.VCC
  N723: Register_65.DS, Register_66.Q7'
  N724: Register_66.MR, Register_66.VCC
  N725: Register_66.DS, Register_68.Q7'
  N726: Register_67.MR, Register_67.VCC
  N727: Register_67.DS, Register_69.Q7'
  N728: Register_68.MR, Register_68.VCC
  N729: Register_68.DS, Register_71.Q7'
  N730: Register_69.MR, Register_69.VCC
  N731: Register_69.DS, Register_70.Q7'
  N732: Register_70.MR, Register_70.VCC
  N733: Register_70.DS, Register_73.Q7'
  N734: Register_71.MR, Register_71.VCC
  N735: Register_71.DS, Register_72.Q7'
  N736: Register_72.MR, Register_72.VCC
  N737: Register_73.MR, Register_73.VCC

notes:
  8
  1
  pin 3 pin 4
  1 2
  15 16
  6 7
  8 9
  5
  4
  pin 1 pin 2
  Serial Number:
  Batch Number:
  JLCJLCJLCJLC
  Electrorchestrion
  Gabriel Peressini
  2020

custom parts:
  STARBOARD_GND: StarBoard ground Pad Starboard pads sans the star cutout in top layer
